# Fritzing sketch HM_10_BT (saved by Fritzing 0.9.3b)
breadboards: 2

parts:
  Part1 = Bluetooth HM-10
  Part3 = Arduino Uno (Rev3) - ICSP
  R1 = Resistor [tolerance=±5% resistance=1k package=THT]
  R2 = Resistor [tolerance=±5% resistance=2.2k package=THT]
  Part4 = Arduino Uno (Rev3) - ICSP
  Part5 = Bluetooth HM-10
  R3 = Resistor [tolerance=±5% resistance=1k package=THT]
  R4 = Resistor [tolerance=±5% resistance=2.2k package=THT]
  R5 = Photocell (LDR) [package=THT]
  R6 = Resistor [tolerance=±5% resistance=10k package=THT]
  LED1 = LED - 5mm [color="Green (555nm)" package="5 mm [THT]"]
  R7 = Resistor [tolerance=±5% resistance=220 package=THT]
  S1 = Pushbutton [package="[THT]"]
  LED2 = LED - 5mm [color="Red (633nm)" package="5 mm [THT]"]
  R8 = Resistor [tolerance=±5% resistance=220 package=THT]
  R9 = Resistor [tolerance=±5% resistance=10k package=THT]

nets:
  N1: Part1.RXD, R1.Pin_0, R2.Pin_1
  N2: Part1.TXD, Part3.D10_PWM/SS
  GND: Part1.GND, Part3.GND, R2.Pin_0, R6.Pin_0, LED1.cathode
  VCC: Part1.VCC, Part3.5V, R5.pin_0
  N3: Part3.A0, R5.pin_1, R6.Pin_1
  N4: Part3.ICSP_MOSI, Part3.D11_PWM/MOSI, R1.Pin_1
  N5: Part3.D2, R7.Pin_1
  N6: Part4.ICSP_MOSI, Part4.D11_PWM/MOSI, R3.Pin_1
  GND_2: Part4.GND, Part5.GND, R4.Pin_0, LED2.cathode, R9.Pin_1
  N7: Part4.D8, S1.Pin_3, S1.Pin_4
  N8: Part4.D10_PWM/SS, Part5.TXD
  N9: Part4.D3_PWM, R8.Pin_1
  5V: Part4.5V, Part5.VCC
  N10: Part5.RXD, R3.Pin_0, R4.Pin_1
  N11: LED1.anode, R7.Pin_0
  N12: S1.Pin_1, S1.Pin_2, R9.Pin_0
  N13: LED2.anode, R8.Pin_0

notes:
  1K
  2.2K
  10K
  220R
