# Fritzing sketch HM_10_BT_BASIC (saved by Fritzing 0.9.3b)
breadboards: 2

parts:
  Part6 = Arduino Uno (Rev3) - ICSP
  Part7 = Arduino Uno (Rev3) - ICSP
  Part8 = Bluetooth HM-10
  Part9 = Bluetooth HM-10
  R10 = Resistor [tolerance=±5% resistance=1k package=THT]
  R11 = Resistor [tolerance=±5% resistance=2.2k package=THT]
  R12 = Resistor [tolerance=±5% resistance=2.2k package=THT]
  R14 = Resistor [tolerance=±5% resistance=1k package=THT]
  LED3 = LED - 5mm [color="Green (555nm)" package="5 mm [THT]"]
  R16 = Resistor [tolerance=±5% resistance=220 package=THT]

nets:
  N1: Part6.ICSP_MOSI, Part6.D11_PWM/MOSI, R14.Pin_1
  N2: Part6.D10_PWM/SS, Part9.TXD
  5V: Part6.5V, Part9.VCC
  GND: Part6.GND, Part9.GND, R11.Pin_0, LED3.cathode
  N3: Part7.ICSP_MOSI, Part7.D11_PWM/MOSI, R10.Pin_1
  N4: Part7.D10_PWM/SS, Part8.TXD
  5V_2: Part7.5V, Part8.VCC
  GND_2: Part7.GND, Part8.GND, R12.Pin_0
  N5: Part8.RXD, R10.Pin_0, R12.Pin_1
  N6: Part9.RXD, R11.Pin_1, R14.Pin_0
  N7: Part9.STATE, R16.Pin_1
  N8: LED3.anode, R16.Pin_0

notes:
  1K
  2.2K
  220R
